# Fritzing sketch Integrador.fzz (saved by Fritzing 0.9.3b)
breadboards: 1

parts:
  Part8 = Arduino Uno (Rev3)
  LED5 = LED - 5mm [color="Red (633nm)" package="5 mm [THT]"]
  LED6 = LED - 5mm [color="Green (555nm)" package="5 mm [THT]"]
  Part9 = KY-033 Tracing Black White Line Hunting Sensor Module For Arduino
  hc-sr3 = hc-sr04
  VCC3 = 4 x AAA Battery Mount
  R4 = Resistor [tolerance=±5% resistance=220 package=THT]
  R5 = Resistor [tolerance=±5% resistance=220 package=THT]
  R6 = Resistor [tolerance=±5% resistance=220 package=THT]
  S2 = Pushbutton [package="[THT]"]
  S3 = H-Bridge with L298N
  M5 = DC Motor
  M6 = DC Motor
  BAT3 = BC9VPC [package=bc9vpc]

nets:
  N1: Part8.A0, Part9.S
  N2: Part8.A5/SCL, hc-sr3.Echo
  N3: Part8.D8, R5.Pin_0
  N4: Part8.D10_PWM/SS, S3.IN2
  N5: Part8.D11_PWM/MOSI, S3.IN1
  N6: Part8.D12/MISO, hc-sr3.Trig
  GND: Part8.GND, VCC3.-, S3.GND
  N7: Part8.D2, R4.Pin_0
  N8: Part8.D3_PWM, R6.Pin_1, S2.Pin_3, S2.Pin_4
  N9: Part8.D5_PWM, S3.IN4
  N10: Part8.D6_PWM, S3.IN3
  N11: Part8.VIN, VCC3.+
  N12: LED5.cathode, R5.Pin_1
  N13: LED5.anode, LED6.anode, Part9.V+, S2.Pin_1, S2.Pin_2
  N14: LED6.cathode, R4.Pin_1
  GND_2: Part9.GND, hc-sr3.GND, R6.Pin_0
  N15: S3.12V, BAT3.V+
  N16: S3.M1-01, M5.pin_2
  N17: S3.M1-02, M5.pin_1
  N18: S3.M2-01, M6.pin_2
  N19: S3.M2-02, M6.pin_1

custom parts:
  KY-033 Tracing Black White Line Hunting Sensor Module For Arduino: Tracing Black White Line Hunting Sensor Module For Arduino Description: This is KY-033 tracking sensor. The KY-033 measures the intensity of infrared radiation and delivers it as an analog output voltage. Features: Operating voltage: 2.5 - 12V(cannot over12V) working current: 18mA-20mA at 5V Enhanced accuracy Documents: http://www.vishay.com/docs/83760/tcrt5000.pdf
  H-Bridge with L298N: h-bridge
