# Fritzing sketch arduino y motores (saved by Fritzing 0.9.3b)

parts:
  S2 = H-Bridge with L298N
  M3 = DC Motor
  M4 = DC Motor
  BAT2 = BC9VPC [package=bc9vpc]
  Part1 = Arduino Uno (Rev3)

nets:
  N1: S2.12V, BAT2.V+
  GND: S2.GND, Part1.GND
  N2: S2.IN1, Part1.D11_PWM/MOSI
  N3: S2.IN2, Part1.D10_PWM/SS
  N4: S2.IN3, Part1.D6_PWM
  N5: S2.IN4, Part1.D5_PWM
  N6: S2.M1-01, M3.pin_2
  N7: S2.M1-02, M3.pin_1
  N8: S2.M2-01, M4.pin_2
  N9: S2.M2-02, M4.pin_1

notes:
  Conexion el arduino y los motores

custom parts:
  H-Bridge with L298N: h-bridge
