# Fritzing sketch arduino y sensores (saved by Fritzing 0.9.3b)
breadboards: 1

parts:
  LED3 = LED - 5mm [color="Red (633nm)" package="5 mm [THT]"]
  LED4 = LED - 5mm [color="Green (555nm)" package="5 mm [THT]"]
  Part6 = KY-033 Tracing Black White Line Hunting Sensor Module For Arduino
  hc-sr2 = hc-sr04
  VCC2 = 4 x AAA Battery Mount
  Part7 = Arduino Uno (Rev3)
  R1 = Resistor [tolerance=±5% resistance=220 package=THT]
  R2 = Resistor [tolerance=±5% resistance=220 package=THT]
  S1 = Pushbutton [package="[THT]"]
  R3 = Resistor [tolerance=±5% resistance=220 package=THT]

nets:
  N1: LED3.cathode, R2.Pin_1
  N2: LED3.anode, LED4.anode, Part6.V+, S1.Pin_1, S1.Pin_2
  N3: LED4.cathode, R1.Pin_1
  GND: Part6.GND, hc-sr2.GND, R3.Pin_0
  N4: Part6.S, Part7.A0
  N5: hc-sr2.Trig, Part7.D12/MISO
  N6: hc-sr2.Echo, Part7.A5/SCL
  N7: VCC2.-, Part7.GND
  N8: VCC2.+, Part7.VIN
  N9: Part7.D8, R2.Pin_0
  N10: Part7.D2, R1.Pin_0
  N11: Part7.D3_PWM, S1.Pin_3, S1.Pin_4, R3.Pin_1

notes:
  Conexion Arduino con seguidor de linea, sensor de distancia, leds, boton y alimentacion

custom parts:
  KY-033 Tracing Black White Line Hunting Sensor Module For Arduino: Tracing Black White Line Hunting Sensor Module For Arduino Description: This is KY-033 tracking sensor. The KY-033 measures the intensity of infrared radiation and delivers it as an analog output voltage. Features: Operating voltage: 2.5 - 12V(cannot over12V) working current: 18mA-20mA at 5V Enhanced accuracy Documents: http://www.vishay.com/docs/83760/tcrt5000.pdf
